# Fritzing sketch Protoshield (saved by Fritzing 0.9.3b)

parts:
  Part1 = Arduino Prototyping Shield
  LM1 = RioRand LM2596  # not connected
  J1 = male pin header, 3 pins [form="♂ (male)"]
  J2 = male pin header, 3 pins [form="♂ (male)"]
  J3 = male pin header, 4 pins [form="♂ (male)"]
  J4 = male pin header, 3 pins [form="♂ (male)"]
  J5 = male pin header, 4 pins [form="♂ (male)"]
  J6 = female pin header, 3 pins [form="♀ (female)"]
  J7 = female pin header, 3 pins [form="♀ (female)"]
  J8 = female pin header, 4 pins [form="♀ (female)"]
  J10 = female pin header, 4 pins [form="♀ (female)"]
  J9 = female pin header, 3 pins [form="♀ (female)"]
  J11 = screw terminal, 2 pins

nets:
  N1: Part1.N$123, J3.pin1, J9.pin1
  N2: Part1.N$191, J4.pin2, J9.pin2
  N3: Part1.N$192, J4.pin1, J9.pin3
  N4: Part1.N$201, J2.pin1, J7.pin1
  N5: Part1.N$203, J3.pin2, J10.pin2
  N6: Part1.N$247, J4.pin3, J10.pin1
  N7: Part1.N$248, J3.pin3, J10.pin4
  N8: Part1.N$249, J3.pin4, J10.pin3
  N9: Part1.N$322, J11.pin2
  N10: Part1.N$325, J5.pin4, J8.pin4
  N11: Part1.N$326, J5.pin3, J8.pin3
  N12: Part1.N$327, J5.pin2, J8.pin2
  N13: Part1.N$366, J5.pin1, J8.pin1
  N14: Part1.N$401, J11.pin1
  N15: Part1.N$428, J1.pin3, J6.pin3
  N16: Part1.N$429, J1.pin2, J6.pin2
  N17: Part1.N$431, J1.pin1, J6.pin1
  N18: Part1.N$434, J2.pin3, J7.pin3
  N19: Part1.N$435, J2.pin2, J7.pin2

notes:
  COIN
  +12V
  GND
  CANCEL BUTTON
  CANCEL LIGHT
  VCC +5V
  SDA
  SCL
  I2C LCD
  CH-92x COIN MECH
  LED PUSH BUTTON
  RST
  3.3V
  MISO
  MOSI
  SCK
  SDA/SS
  RC522 RFID READER
  POWER INPUT
